# Fritzing sketch sketch-v0-2-x (saved by Fritzing 0.9.4)
breadboards: 1

parts:
  Part1 = Arduino Uno (Rev3) - ICSP
  U1 = ESP8266 WiFi Module [part_number=ESP8266]
  U2 = Voltage Regulator - 3.3V [package="TO220 [THT]"]
  LED1 = smd LED [color="Red (633nm)" package="1206 [SMD]"]
  LED2 = smd LED [color="Yellow (595nm)" package="1206 [SMD]"]
  LED3 = smd LED [color="Green (555nm)" package="1206 [SMD]"]
  R1 = Resistor [tolerance=±5% resistance=1k package="0603 [SMD]"]
  R2 = Resistor [tolerance=±5% resistance=1k package="0603 [SMD]"]
  R3 = Resistor [tolerance=±5% resistance=1k package="0603 [SMD]"]
  LED4 = smd LED [color="Blue (430nm)" package="1206 [SMD]"]
  R4 = Resistor [tolerance=±5% resistance=1k package="0603 [SMD]"]
  Part3 = IMU Digital Combo Board 6DOF
  Part4 = IMU Digital Combo Board 6DOF
  Part6 = IMU Digital Combo Board 6DOF
  WeMos_D1_Mini_Relay_Shield_V1 = WeMos D1 Mini Relay Shield V2

nets:
  N1: Part1.D8, Part3.INT0
  N2: Part1.D10_PWM/SS, U1.IO0
  N3: Part1.D11_PWM/MOSI, U1.IO14
  N4: Part1.D12/MISO, LED4.cathode
  N5: Part1.GND, U1.IO15, U2.input_voltage, R1.Pin_1, R2.Pin_1, R3.Pin_1, R4.Pin_1, Part3.SCL, WeMos_D1_Mini_Relay_Shield_V1.G
  N6: Part1.D2, LED3.cathode
  N7: Part1.D3_PWM, LED2.cathode
  N8: Part1.D4, LED1.cathode
  N9: Part1.D5_PWM, WeMos_D1_Mini_Relay_Shield_V1.3V3
  N10: Part1.D6_PWM, Part6.INT0
  N11: Part1.D7, Part4.INT0
  N12: Part1.5V, U2.output_voltage, Part3.INT1, Part4.SCL, Part4.INT1, Part6.SCL, Part6.INT1, WeMos_D1_Mini_Relay_Shield_V1.D4
  N13: U1.IO2, U1.CLK, U2.GND
  N14: LED1.anode, R3.Pin_0
  N15: LED2.anode, R2.Pin_0
  N16: LED3.anode, R1.Pin_0
  N17: LED4.anode, R4.Pin_0

notes:
  ESP8266 ESP-01
  TXD -> D10 (Rx)
  CHP0 -> 3.3v
  RTS -> nil
  VCC -> 3.3v
  GND -> GND
  GP2 -> nil
  GP0 -> nil
  RX0 -> D11 (Tx)
  http://192.168.4.1
  "/": "Welcome message",
  "/status": "Current state of subsystems"
  "/led": "Current state of LED - On/Off"
  "/led/toggle": "Toggle LED On/Off"
  Contact Water Level Sensors
  High, Mid, Low water levels
  Voltage Regulator
  LV1117AV33
  Converts 5v from Ardunio to
  stable 3.3v as required by
  ESP8266 ESP-01
  5v - red
  3.3v - orange
  LEDs
  - blue: test case for on/off
  - red: water level low
  - yellow: water level mid
  - green: water level full
  pump control
  normally closed, pump will not operate until relay is enabled
